# Fritzing sketch Op-amp (saved by Fritzing 0.9.3b)
breadboards: 1

parts:
  IC1 = IC, DIP package, 8 pins [chip_label=6002]
  R1 = Resistor [tolerance=±5% resistance=220 package=THT]
  R2 = Resistor [tolerance=±5% resistance=220 package=THT]

nets:
  N1: IC1.pin2, R1.Pin_1, R2.Pin_0
  N2: IC1.pin4, R2.Pin_1

notes:
  5V
  Output
  0V
  Inverting input
  Non Inverting input
