# Fritzing sketch bumpSwitch (saved by Fritzing 0.9.3b)
breadboards: 1

parts:
  S1 = Toggle Switch [package=THT]
  R1 = Resistor [tolerance=±5% resistance=10k package=THT]

nets:
  N1: S1.L1, R1.Pin_1

notes:
  0V
  Output
  5V
